// Logisim project add-impl.circ as structural Verilog: 1 circuit, main circuit main
module main (
  input  a,
  input  b,
  input  cin,
  output cout,
  output s
);


  // Notes on the sheet:
  //   Build a full adder using basic logic gates
endmodule
