// Logisim project add-spec.circ as structural Verilog: 1 circuit, main circuit main
module main (
  input  a,
  input  b,
  input  cin,
  output cout,
  output s
);

  Adder #(.width(1)) adder_1 (.a(a), .b(b), .out(s), .cin(cin), .cout(cout));
endmodule
