// Logisim project add-tb.circ as structural Verilog: 1 circuit, main circuit main
module main (
  output a,
  output b,
  output cin,
  output cout,
  output s,
  output halt
);

  wire clock_1_out;

  Clock clock_1 (.out(clock_1_out));
  Counter #(.width(4), .max('hf)) counter_1 (
    .Q({halt, cin, b, a}), .clk(clock_1_out));  // open: load, D, count, carry, clr
  add_impl_main main_1 (.a(a), .b(b), .cin(cin), .s(s), .cout(cout));
endmodule
