// Logisim project addsub-impl.circ as structural Verilog: 1 circuit, main circuit main
module main (
  input  [7:0] A,
  input  [7:0] B,
  input  sub,
  output [7:0] Y
);


  // Notes on the sheet:
  //   Build an adder-subtractor using one 8 bit adder
endmodule
