// Logisim project addsub-tb.circ as structural Verilog: 1 circuit, main circuit main
module main (
  output [7:0] A,
  output [7:0] B,
  output sub,
  output [7:0] Y,
  output halt
);

  wire clock_1_out;
  wire [2:0] counter_1_q;

  Clock clock_1 (.out(clock_1_out));
  Counter #(.width(5), .max('h1f)) counter_1 (
    .Q({halt, sub, counter_1_q}), .clk(clock_1_out));  // open: load, D, count, carry, clr
  ROM #(.addrWidth(3)) rom_1 (.addr(counter_1_q), .data(A));  // open: sel
  ROM #(.addrWidth(3)) rom_2 (.addr(counter_1_q), .data(B));  // open: sel
  addsub_impl_main main_1 (.A(A), .B(B), .sub(sub), .Y(Y));

  // Notes on the sheet:
  //   contents of rom_1 (hex, n*v repeats v):
  //   1 2 80 b2 ff 10 20 40
  //   contents of rom_2 (hex, n*v repeats v):
  //   0 1 3f ff 80 10 30 80
endmodule
