// Logisim project alu-tb.circ as structural Verilog: 1 circuit, main circuit main
module main (
  output clk,
  output [7:0] A,
  output [7:0] A_prime,
  output [7:0] B,
  output [7:0] B_prime,
  output [2:0] op,
  output [7:0] Res,
  output [7:0] Res_prime,
  output halt
);

  wire clock_1_out;
  wire [4:0] counter_1_q;

  not not_1 (clk, clock_1_out);
  Clock clock_1 (.out(clock_1_out));
  Counter #(.width(6), .max('h3f)) counter_1 (.Q({halt, counter_1_q}), .clk(clk));  // open: load, D, count, carry, clr
  ROM #(.addrWidth(5)) rom_1 (.addr(counter_1_q), .data(A));  // open: sel
  ROM #(.addrWidth(5)) rom_2 (.addr(counter_1_q), .data(B));  // open: sel
  ROM #(.addrWidth(5), .dataWidth(3)) rom_3 (.addr(counter_1_q), .data(op));  // open: sel
  ALU alu_1 (.A(A), .B(B), .Res(Res), .op(op));

  assign A_prime = A;
  assign B_prime = B;
  assign Res_prime = Res;

  // Notes on the sheet:
  //   contents of rom_1 (hex, n*v repeats v):
  //   1 2 ff 1 ff aa 33 bb 1 0 ff 10 1 0 ff 10 aa ff 0 10 ff aa 33 bb aa ff 10 7 ff f0 f aa
  //   contents of rom_2 (hex, n*v repeats v):
  //   1 2 1 1f 1 2 3 4 0 ff 10 f 1 8 ff 10 ff a aa 1 1 2 3 4 33 11 1 f0 a a 3 55
  //   contents of rom_3 (hex, n*v repeats v):
  //   4*0 4*1 4*2 4*3 4*4 4*5 4*6 4*7
endmodule
