// Logisim project alu.circ as structural Verilog: 1 circuit, main circuit ALU
module ALU (
  input  [7:0] A,
  input  [7:0] B,
  input  [2:0] op,
  output [7:0] Res
);


  // Notes on the sheet:
  //   Build the ALU!
endmodule
