// Logisim project counter-impl.circ as structural Verilog: 2 circuits, main circuit main
module main (
  input  clk,
  input  reset,
  output [3:0] count
);


  // Notes on the sheet:
  //   Build a counter
endmodule

module sim (
);

  wire button_1_out, clock_1_out;
  wire [3:0] main_1_count;

  Button button_1 (.out(button_1_out));
  main main_1 (.clk(clock_1_out), .count(main_1_count), .reset(button_1_out));
  Clock clock_1 (.out(clock_1_out));
  Hex_Digit_Display hex_digit_display_1 (.value(main_1_count));  // open: dp
endmodule
