// Logisim project counter-tb.circ as structural Verilog: 1 circuit, main circuit main
module main (
  output clk,
  output reset,
  output [3:0] count,
  output halt
);

  wire not_1_out;
  wire [5:0] counter_1_q;

  Clock clock_1 (.out(clk));
  not not_1 (not_1_out, clk);
  Counter #(.width(7), .max('h7f)) counter_1 (
    .Q({halt, counter_1_q}), .clk(not_1_out));  // open: load, D, count, carry, clr
  counter_impl_main main_1 (.clk(clk), .count(count), .reset(reset));
  Comparator #(.width(7)) comparator_1 (.a({halt, counter_1_q}), .b({7{1'b0}}), .eq(reset));  // open: gt, lt
endmodule
