// Logisim project dec-impl.circ as structural Verilog: 1 circuit, main circuit main
module main (
  input  E0,
  input  E1,
  output S0,
  output S1,
  output S2,
  output S3
);


  // Notes on the sheet:
  //   Build a 2-to-4 decoder using basic logic gates
endmodule
