// Logisim project dec-spec.circ as structural Verilog: 1 circuit, main circuit main
module main (
  input  E0,
  input  E1,
  output S0,
  output S1,
  output S2,
  output S3
);

  Decoder #(.select(2), .enable("false")) decoder_1 (.out0(S0), .out1(S1), .out2(S2), .out3(S3), .sel({E1, E0}));
endmodule
