// Logisim project dec-tb.circ as structural Verilog: 1 circuit, main circuit main
module main (
  output E0,
  output E1,
  output S0,
  output S1,
  output S2,
  output S3,
  output halt
);

  wire clock_1_out;

  Counter #(.width(3), .max('h7)) counter_1 (
    .Q({halt, E1, E0}), .clk(clock_1_out));  // open: load, D, count, carry, clr
  Clock clock_1 (.out(clock_1_out));
  dec_impl_main main_1 (.E0(E0), .E1(E1), .S0(S0), .S1(S1), .S2(S2), .S3(S3));
endmodule
