// Logisim project dff-spec.circ as structural Verilog: 2 circuits, main circuit main
module main (
  input  clk,
  input  reset,
  input  D,
  input  en,
  output Q
);

  wire and_1_out;

  and and_1 (and_1_out, ~reset, D);  // AND_Gate
  D_Flip_Flop d_ff_1 (.clk(clk), .D(and_1_out), .Q(Q), .en(en));  // open: Qn, preset, reset
endmodule

module sim (
  input  D,
  input  reset,
  input  en
);

  wire clk_out, main_1_q;

  Clock clk (.out(clk_out));
  main main_1 (.clk(clk_out), .reset(reset), .D(D), .en(en), .Q(main_1_q));
  LED Q (.in(main_1_q));
endmodule
