// Logisim project dff-tb.circ as structural Verilog: 1 circuit, main circuit main
module main (
  output clk,
  output reset,
  output en,
  output D,
  output Q,
  output halt
);

  wire not_1_out;
  wire [3:0] counter_1_q;

  Counter #(.width(5), .max('h1f)) counter_1 (
    .Q({halt, counter_1_q}), .clk(not_1_out));  // open: load, D, count, carry, clr
  not not_1 (not_1_out, clk);
  Clock clock_1 (.out(clk));
  ROM #(.addrWidth(4), .dataWidth(3)) rom_1 (.addr(counter_1_q), .data({en, reset, D}));  // open: sel
  dff_impl_main main_1 (.clk(clk), .reset(reset), .D(D), .en(en), .Q(Q));

  // Notes on the sheet:
  //   contents of rom_1 (hex, n*v repeats v):
  //   2 2 4 5 4 0 1 1 5 1 1 0 4 4 5 1
endmodule
