// Logisim project edgedetect-impl.circ as structural Verilog: 2 circuits, main circuit main
module main (
  input  D,
  input  clk,
  output TOP
);


  // Notes on the sheet:
  //   Build a rising edge detector
endmodule

module sim (
);

  wire button_1_out, clock_1_out, main_1_top;

  Button button_1 (.out(button_1_out));
  main main_1 (.D(button_1_out), .clk(clock_1_out), .TOP(main_1_top));
  Clock clock_1 (.out(clock_1_out));
  LED led_1 (.in(main_1_top));
endmodule
