// Logisim project edgedetect-spec.circ as structural Verilog: 2 circuits, main circuit main
module main (
  input  D,
  input  clk,
  output TOP
);

  wire d_ff_1_q, d_ff_2_q;

  D_Flip_Flop d_ff_1 (.clk(clk), .D(D), .Q(d_ff_1_q));  // open: Qn, preset, en, reset
  D_Flip_Flop d_ff_2 (.clk(clk), .D(d_ff_1_q), .Q(d_ff_2_q));  // open: Qn, preset, en, reset
  and and_1 (TOP, d_ff_1_q, ~d_ff_2_q);  // AND_Gate

  // Notes on the sheet:
  //   Build a rising edge detector
endmodule

module sim (
);

  wire button_1_out, clock_1_out, main_1_top;

  Button button_1 (.out(button_1_out));
  main main_1 (.D(button_1_out), .clk(clock_1_out), .TOP(main_1_top));
  Clock clock_1 (.out(clock_1_out));
  LED led_1 (.in(main_1_top));
endmodule
