// Logisim project edgedetect-tb.circ as structural Verilog: 1 circuit, main circuit main
module main (
  output clk,
  output D,
  output TOP,
  output halt
);

  wire not_1_out;
  wire [4:0] counter_1_q;

  not not_1 (not_1_out, clk);
  Counter #(.width(6), .max('h3f)) counter_1 (
    .Q({halt, counter_1_q}), .clk(not_1_out));  // open: load, D, count, carry, clr
  edgedetect_impl_main main_1 (.D(D), .clk(clk), .TOP(TOP));
  ROM #(.addrWidth(5), .dataWidth(1)) rom_1 (.addr(counter_1_q), .data(D));  // open: sel
  Clock clock_1 (.out(clk));

  // Notes on the sheet:
  //   contents of rom_1 (hex, n*v repeats v):
  //   4*0 4*1 4*0 7*1 0 0 0 1 0 0 1 1 0 0 1
endmodule
