// Logisim project fsm-solution.circ as structural Verilog: 2 circuits, main circuit main
module main (
  input  clk,
  input  reset,
  input  button,
  output LED0,
  output LED1
);

  wire and_1_out, S0, S0_prime, S1, S1_prime, top;

  // edgedetect_main main_1: pin names not known; wires that end beside it: button, clk, top
  D_Flip_Flop u_S0 (.clk(clk), .D(S0_prime), .Q(S0), .reset(reset));  // open: Qn, preset, en
  D_Flip_Flop u_S1 (.clk(clk), .D(S1_prime), .Q(S1), .reset(reset));  // open: Qn, preset, en
  and and_1 (and_1_out, S0, top);
  and and_2 (LED0, S0, ~S1);  // AND_Gate
  and and_3 (LED1, S1, S0);
  xor xor_1 (S0_prime, top, S0);
  xor xor_2 (S1_prime, and_1_out, S1);

  // Notes on the sheet:
  //   Implement the FSM
endmodule

module sim (
  input  in_1
);

  wire button_1_out, clock_1_out, main_1_led0, main_1_led1;

  Button button_1 (.out(button_1_out));
  main main_1 (.button(button_1_out), .clk(clock_1_out), .reset(in_1), .LED0(main_1_led0), .LED1(main_1_led1));
  Clock clock_1 (.out(clock_1_out));
  LED led_1 (.in(main_1_led0));
  LED led_2 (.in(main_1_led1));
endmodule
