// Logisim project max-solution.circ as structural Verilog: 2 circuits, main circuit max-8
module max_8 (
  input  [7:0] A,
  input  [7:0] B,
  output [7:0] M
);

  wire main_1_a_bout, main_1_b_aout, main_2_a_bout, main_2_b_aout, main_3_a_bout, main_3_b_aout,
       main_4_a_bout, main_4_b_aout, main_5_a_bout, main_5_b_aout, main_6_a_bout, main_6_b_aout,
       main_7_a_bout, main_7_b_aout;

  main main_1 (
    .a(A[7]), .b(B[7]), .A_Bin(1'b0), .B_Ain(1'b0), .m(M[7]), .A_Bout(main_1_a_bout), .B_Aout(main_1_b_aout));
  main main_2 (
    .a(A[6]), .b(B[6]), .A_Bin(main_1_a_bout), .B_Ain(main_1_b_aout), .m(M[6]), .A_Bout(main_2_a_bout),
    .B_Aout(main_2_b_aout));
  main main_3 (
    .a(A[5]), .b(B[5]), .A_Bin(main_2_a_bout), .B_Ain(main_2_b_aout), .m(M[5]), .A_Bout(main_3_a_bout),
    .B_Aout(main_3_b_aout));
  main main_4 (
    .a(A[4]), .b(B[4]), .A_Bin(main_3_a_bout), .B_Ain(main_3_b_aout), .m(M[4]), .A_Bout(main_4_a_bout),
    .B_Aout(main_4_b_aout));
  main main_5 (
    .a(A[3]), .b(B[3]), .A_Bin(main_4_a_bout), .B_Ain(main_4_b_aout), .m(M[3]), .A_Bout(main_5_a_bout),
    .B_Aout(main_5_b_aout));
  main main_6 (
    .a(A[2]), .b(B[2]), .A_Bin(main_5_a_bout), .B_Ain(main_5_b_aout), .m(M[2]), .A_Bout(main_6_a_bout),
    .B_Aout(main_6_b_aout));
  main main_7 (
    .a(A[1]), .b(B[1]), .A_Bin(main_6_a_bout), .B_Ain(main_6_b_aout), .m(M[1]), .A_Bout(main_7_a_bout),
    .B_Aout(main_7_b_aout));
  main main_8 (.a(A[0]), .b(B[0]), .A_Bin(main_7_a_bout), .B_Ain(main_7_b_aout), .m(M[0]));  // open: A_Bout, B_Aout
endmodule

module main (
  input  a,
  input  b,
  input  A_Bin,
  input  B_Ain,
  output m,
  output A_Bout,
  output B_Aout
);

  wire and_1_out, and_2_out, and_3_out, and_4_out, and_5_out, or_1_out;

  or or_1 (or_1_out, a, b);
  or or_2 (A_Bout, A_Bin, and_1_out);
  and and_1 (and_1_out, ~B_Ain, a, ~b);  // AND_Gate
  and and_2 (and_2_out, ~a, b, ~A_Bin);  // AND_Gate
  or or_3 (B_Aout, and_2_out, B_Ain);
  and and_3 (and_3_out, a, A_Bout);
  and and_4 (and_4_out, b, B_Aout);
  and and_5 (and_5_out, or_1_out, ~A_Bout, ~B_Aout);  // AND_Gate
  or or_4 (m, and_3_out, and_4_out, and_5_out);
endmodule
