// Logisim project mux-impl.circ as structural Verilog: 1 circuit, main circuit main
module main (
  input  DIN0,
  input  DIN1,
  input  Sel,
  output DOUT
);


  // Notes on the sheet:
  //   Build a 2-1 MUX using basic logic gates
endmodule
