// Logisim project mux-spec.circ as structural Verilog: 1 circuit, main circuit main
module main (
  input  DIN0,
  input  DIN1,
  input  Sel,
  output DOUT
);

  Multiplexer #(.enable("false")) multiplexer_1 (.in0(DIN0), .in1(DIN1), .out(DOUT), .sel(Sel));
endmodule
