// Logisim project mux-tb.circ as structural Verilog: 1 circuit, main circuit main
module main (
  output DIN0,
  output DIN1,
  output Sel,
  output DOUT,
  output halt
);

  wire clock_1_out;

  Clock clock_1 (.out(clock_1_out));
  Counter #(.width(4), .max('hf)) counter_1 (
    .Q({halt, Sel, DIN1, DIN0}), .clk(clock_1_out));  // open: load, D, count, carry, clr
  mux_impl_main main_1 (.DIN0(DIN0), .DIN1(DIN1), .Sel(Sel), .DOUT(DOUT));
endmodule
