// Logisim project reg-impl.circ as structural Verilog: 1 circuit, main circuit main
module main (
  input  clk,
  input  reset,
  input  [1:0] addr,
  input  [7:0] din,
  input  write,
  output [7:0] dout
);

  Register register_1 ();  // open: D, en, Q, clk, clr
  Register register_2 ();  // open: D, en, Q, clk, clr
  Register register_3 ();  // open: D, en, Q, clk, clr
  Register register_4 ();  // open: D, en, Q, clk, clr

  // Notes on the sheet:
  //   Build an addressable register bank
  //   Reg 0
  //   Reg 1
  //   Reg 2
  //   Reg 3
endmodule
