// Logisim project reg-spec.circ as structural Verilog: 1 circuit, main circuit main
module main (
  input  clk,
  input  reset,
  input  [1:0] addr,
  input  [7:0] din,
  input  write,
  output [7:0] dout
);

  RAM #(.addrWidth(2), .bus("separate")) ram_1 (
    .addr(addr), .din(din), .data(dout), .str(write), .clk(clk), .ld(1'b1), .clr(reset));  // open: sel
endmodule
