// Logisim project reg-tb.circ as structural Verilog: 1 circuit, main circuit main
module main (
  output clk,
  output reset,
  output write,
  output [1:0] addr,
  output [7:0] din,
  output [7:0] dout,
  output halt
);

  wire not_1_out;
  wire [3:0] counter_1_q;

  Clock clock_1 (.out(clk));
  Counter #(.width(5), .max('h1f), .ongoal("stay")) counter_1 (
    .Q({halt, counter_1_q}), .clk(not_1_out));  // open: load, D, count, carry, clr
  not not_1 (not_1_out, clk);
  ROM #(.addrWidth(4), .dataWidth(12)) rom_1 (.addr(counter_1_q), .data({din, addr, write, reset}));  // open: sel
  reg_impl_main main_1 (.clk(clk), .reset(reset), .din(din), .write(write), .dout(dout), .addr(addr));

  // Notes on the sheet:
  //   contents of rom_1 (hex, n*v repeats v):
  //   1 0 aa2 aa0 0 426 246 ff4 ff0 99e 990 d 77a 8 0 4
endmodule
