// Logisim project ser2par-impl.circ as structural Verilog: 2 circuits, main circuit main
module main (
  input  Sin,
  input  clk,
  input  reset,
  output [3:0] Pout,
  output valid
);


  // Notes on the sheet:
  //   Build a serial-to-parallel converter
endmodule

module sim (
  input  in_1
);

  wire button_1_out, clock_1_out, main_1_valid;
  wire [3:0] main_1_pout;

  main main_1 (.Sin(in_1), .clk(clock_1_out), .Pout(main_1_pout), .valid(main_1_valid), .reset(button_1_out));
  Clock clock_1 (.out(clock_1_out));
  Button button_1 (.out(button_1_out));
  Hex_Digit_Display hex_digit_display_1 (.value(main_1_pout), .dp(main_1_valid));
endmodule
