// Logisim project ser2par-spec.circ as structural Verilog: 2 circuits, main circuit main
module main (
  input  Sin,
  input  clk,
  input  reset,
  output [3:0] Pout,
  output valid
);

  wire shift_register_2_out;

  Shift_Register #(.length(4)) shift_register_1 (
    .in(Sin), .clk(clk), .clr(reset), .q0(Pout[3]), .q1(Pout[2]), .q2(Pout[1]), .q3(Pout[0]));  // open: shift, out, load, d0, d1, d2, d3
  Shift_Register #(.length(4)) shift_register_2 (
    .in(shift_register_2_out), .clk(clk), .out(shift_register_2_out), .load(reset), .d0(1'b1), .d1(1'b0),
    .d2(1'b0), .d3(1'b0));  // open: shift, clr, q0, q1, q2, q3
  D_Flip_Flop d_ff_1 (.clk(clk), .D(shift_register_2_out), .Q(valid), .reset(reset));  // open: Qn, preset, en

  // Notes on the sheet:
  //   Build a serial-to-parallel converter
endmodule

module sim (
  input  in_1
);

  wire button_1_out, clock_1_out, main_1_valid;
  wire [3:0] main_1_pout;

  main main_1 (.Sin(in_1), .clk(clock_1_out), .Pout(main_1_pout), .valid(main_1_valid), .reset(button_1_out));
  Button button_1 (.out(button_1_out));
  Clock clock_1 (.out(clock_1_out));
  Hex_Digit_Display hex_digit_display_1 (.value(main_1_pout), .dp(main_1_valid));
endmodule
