// Logisim project ser2par-tb.circ as structural Verilog: 1 circuit, main circuit main
module main (
  output clk,
  output reset,
  output Sin,
  output [3:0] Pout,
  output valid,
  output halt
);

  wire not_1_out;
  wire [4:0] counter_1_q;

  Counter #(.width(6), .max('h3f)) counter_1 (
    .Q({halt, counter_1_q}), .clk(not_1_out));  // open: load, D, count, carry, clr
  not not_1 (not_1_out, clk);
  Clock clock_1 (.out(clk));
  ROM #(.addrWidth(5), .dataWidth(1)) rom_1 (.addr(counter_1_q), .data(Sin));  // open: sel
  Comparator #(.width(5), .mode("unsigned")) comparator_1 (.a(counter_1_q), .b(5'b00100), .lt(reset));  // open: gt, eq
  ser2par_impl_main main_1 (.Sin(Sin), .clk(clk), .Pout(Pout), .valid(valid), .reset(reset));

  // Notes on the sheet:
  //   contents of rom_1 (hex, n*v repeats v):
  //   4*0 1 0 1 0 0 0 4*1 0 5*1 0 0 4*1 0 0 0 1
endmodule
