// Logisim project sub-impl.circ as structural Verilog: 1 circuit, main circuit main
module main (
  input  a,
  input  b,
  input  cin,
  output cout,
  output d
);


  // Notes on the sheet:
  //   Build a subtractor using basic logic gates
endmodule
