// Logisim project sub-spec.circ as structural Verilog: 1 circuit, main circuit main
module main (
  input  a,
  input  b,
  input  cin,
  output cout,
  output d
);

  Subtractor #(.width(1)) subtractor_1 (.a(a), .b(b), .out(d), .bin(cin), .bout(cout));
endmodule
